// Logisim project cpu.circ as structural Verilog: 3 circuits, main circuit main
module main (
);

  wire AC_LD, AR_LD, CLK, DR_INC, DR_LD, IR_LD, MEM_READ, MEM_WRITE, PC_INC, PC_LD;
  wire [2:0] C2C1C0, S2S1S0;
  wire [7:0] AR_q, bit_extender_1_out, bit_extender_2_out, PC_q;
  wire [15:0] AC_q, alu_1_output, bit_extender_3_out, bit_extender_4_out, bit_extender_5_out, DR, IR,
       multiplexer_1_out, ram_1_data, TR_q;

  Clock clock_1 (.out(CLK));
  Bit_Extender #(.in_width(16), .out_width(8)) bit_extender_1 (.in(multiplexer_1_out), .out(bit_extender_1_out));
  Bit_Extender #(.in_width(16), .out_width(8)) bit_extender_2 (.in(multiplexer_1_out), .out(bit_extender_2_out));
  ALU alu_1 (.DR(DR), .AC(AC_q), .Output(alu_1_output));
  Counter AR (.load(AR_LD), .D(bit_extender_1_out), .count(1'b0), .Q(AR_q), .clk(CLK), .clr(1'b0));  // open: carry
  Counter PC (.load(PC_LD), .D(bit_extender_2_out), .count(PC_INC), .Q(PC_q), .clk(CLK), .clr(1'b0));  // open: carry
  Counter #(.width(16), .max('hffff)) u_DR (
    .load(DR_LD), .D(multiplexer_1_out), .count(DR_INC), .Q(DR), .clk(CLK), .clr(1'b0));  // open: carry
  Counter #(.width(16), .max('hffff)) AC (
    .load(AC_LD), .D(alu_1_output), .count(1'b0), .Q(AC_q), .clk(CLK), .clr(1'b0));  // open: carry
  Register #(.width(16)) u_IR (.D(multiplexer_1_out), .en(IR_LD), .Q(IR), .clk(CLK), .clr(1'b0));
  Register #(.width(16)) TR (.D(multiplexer_1_out), .en(1'b0), .Q(TR_q), .clk(CLK), .clr(1'b0));
  RAM #(.dataWidth(16), .bus("separate")) ram_1 (
    .addr(AR_q), .din(multiplexer_1_out), .data(ram_1_data), .str(MEM_WRITE), .clk(CLK), .ld(MEM_READ));  // open: sel, clr
  assign bit_extender_3_out = {{8{1'b0}}, AR_q};  // Bit_Extender bit_extender_3
  assign bit_extender_4_out = {{8{1'b0}}, PC_q};  // Bit_Extender bit_extender_4
  assign bit_extender_5_out = {{8{1'b0}}, IR[11:4]};  // Bit_Extender bit_extender_5
  Multiplexer #(.select(3), .width(16), .enable("false")) multiplexer_1 (
    .in1(ram_1_data), .in2(bit_extender_3_out), .in3(bit_extender_4_out), .in4(DR), .in5(AC_q),
    .in6(bit_extender_5_out), .in7(TR_q), .out(multiplexer_1_out), .sel(S2S1S0));  // open: in0
  CU cu_1 (
    .DR(DR), .IR(IR), .MEM_READ(MEM_READ), .AC_LD(AC_LD), .DR_LD(DR_LD), .PC_LD(PC_LD), .DR_INC(DR_INC),
    .IR_LD(IR_LD), .PC_INC(PC_INC), .C2C1C0(C2C1C0), .MEM_WRITE(MEM_WRITE), .CLK(CLK), .S2S1S0(S2S1S0),
    .AR_LD(AR_LD));
endmodule

module ALU (
  input  [15:0] DR,
  input  [15:0] AC,
  output [15:0] Output
);

  wire [2:0] C2C1C0;
  wire [15:0] adder_1_out, divider_1_out, multiplier_1_out, not_1_out, subtractor_1_out, xor_1_out;

  Divider #(.width(16)) divider_1 (.a(DR), .b(AC), .out(divider_1_out));  // open: upper, rem
  Adder #(.width(16)) adder_1 (.a(DR), .b(AC), .out(adder_1_out));  // open: cin, cout
  Subtractor #(.width(16)) subtractor_1 (.a(DR), .b(AC), .out(subtractor_1_out));  // open: bin, bout
  Multiplier #(.width(16)) multiplier_1 (.a(DR), .b(AC), .out(multiplier_1_out));  // open: cin, cout
  assign not_1_out = ~DR;  // NOT_Gate not_1, 16 bits wide
  assign xor_1_out = DR ^ AC;  // XOR_Gate xor_1, 16 bits wide
  Multiplexer #(.select(3), .width(16), .enable("false")) multiplexer_1 (
    .in1(DR), .in2(adder_1_out), .in3(subtractor_1_out), .in4(multiplier_1_out), .in5(divider_1_out),
    .in6(not_1_out), .in7(xor_1_out), .out(Output), .sel(C2C1C0));  // open: in0
endmodule

module CU (
  input  [15:0] IR,
  input  CLK,
  input  [15:0] DR,
  output MEM_READ,
  output AC_LD,
  output MEM_WRITE,
  output DR_LD,
  output PC_LD,
  output DR_INC,
  output AR_LD,
  output IR_LD,
  output PC_INC,
  output [2:0] S2S1S0,
  output [2:0] C2C1C0
);

  wire ADD_out, and_1_out, and_2_out, and_3_out, and_4_out, and_5_out, and_9_out, and_10_out, and_11_out,
       and_12_out, and_13_out, and_14_out, and_15_out, and_16_out, and_17_out, and_18_out, and_19_out,
       and_20_out, and_21_out, and_22_out, and_23_out, CLRSC, D0, D1, D2, D3, D4, D5, D6, D_FF_q, DIV_out,
       DR_ZERO, LDA_out, MEM_out, or_1_out, or_5_out, or_6_out, or_9_out, or_10_out, or_11_out, T0, T2, T3,
       T4, T5, T6, XOR_out;
  wire [2:0] sequence_counter_q;

  or or_1 (or_1_out, D0, D2, D3, D4);
  and and_1 (and_1_out, T3, D0);
  and and_2 (and_2_out, T3, D2);
  and and_3 (and_3_out, T3, D4);
  and and_4 (and_4_out, T3, D3);
  and and_5 (and_5_out, T3, D5);
  and and_6 (PC_LD, T3, D6);
  and and_7 (DR_INC, T4, D5);
  and and_8 (AC_LD, T4, or_1_out);
  or or_2 (AR_LD, T0, T2);
  and and_9 (and_9_out, T6, D5, DR_ZERO);
  or or_3 (PC_INC, IR_LD, and_9_out);
  or or_4 (DR_LD, and_1_out, and_2_out, and_3_out, and_4_out, and_5_out);
  and LDA (LDA_out, D0, T4);
  and ADD (ADD_out, D2, T4);
  and DIV (DIV_out, D3, T4);
  and XOR (XOR_out, D4, T4);
  or or_5 (or_5_out, DR[0], DR[1], DR[2], DR[3], DR[4], DR[5], DR[7], DR[6], DR[8], DR[9], DR[10], DR[11], DR[12], DR[13], DR[14], DR[15]);
  Priority_Encoder priority_encoder_1 (
    .in0(1'b0), .in1(LDA_out), .in2(ADD_out), .in3(1'b0), .in4(1'b0), .in5(DIV_out), .in6(1'b0),
    .in7(XOR_out), .out(C2C1C0));  // open: en_in, gs, en_out
  not not_1 (DR_ZERO, or_5_out);
  or or_6 (or_6_out, D0, D2, D4, D3, D5);
  and and_10 (and_10_out, T3, D1);
  and and_11 (and_11_out, T5, D5);
  and and_12 (and_12_out, T3, or_6_out);
  or or_7 (MEM_READ, IR_LD, and_12_out);
  or or_8 (MEM_WRITE, and_10_out, and_11_out);
  or or_9 (or_9_out, D0, D2, D3, D4, D5);
  or or_10 (or_10_out, D0, D2, D3, D4);
  and and_13 (and_13_out, T3, or_9_out);
  and and_14 (and_14_out, T4, or_10_out);
  and and_15 (and_15_out, D5, T5);
  and and_16 (and_16_out, T3, D1);
  and and_17 (and_17_out, T4, D2);
  and and_18 (and_18_out, T4, D3);
  and and_19 (and_19_out, T4, D4);
  and and_20 (and_20_out, T6, D5);
  or MEM (MEM_out, IR_LD, and_13_out);
  or or_11 (or_11_out, and_14_out, and_15_out);
  or or_12 (CLRSC, and_23_out, and_16_out, and_17_out, and_18_out, and_19_out, and_20_out, and_21_out);
  and and_21 (and_21_out, T3, D6);
  and and_22 (and_22_out, D1, T3);
  and and_23 (and_23_out, T4, D0);
  Counter #(.width(3), .max('h7)) sequence_counter (
    .load(1'b0), .count(1'b1), .Q(sequence_counter_q), .clk(CLK), .clr(D_FF_q));  // open: D, carry
  D_Flip_Flop D_FF (.clk(CLK), .D(CLRSC), .Q(D_FF_q));  // open: Qn, preset, en, reset
  Decoder #(.select(3), .enable("false")) decoder_1 (
    .out0(D0), .out2(D1), .out3(D2), .out4(D3), .out5(D4), .out6(D5), .out7(D6), .sel(IR[14:12]));  // open: out1
  Decoder #(.select(3), .enable("false")) decoder_2 (
    .out0(T0), .out1(IR_LD), .out2(T2), .out3(T3), .out4(T4), .out5(T5), .out6(T6), .sel(sequence_counter_q));  // open: out7
  Priority_Encoder priority_encoder_2 (
    .in0(1'b0), .in1(MEM_out), .in2(1'b0), .in3(T0), .in4(or_11_out), .in5(and_22_out), .in6(T2), .in7(1'b0),
    .out(S2S1S0));  // open: en_in, gs, en_out

  // Other names for the same wires on the sheet: DR_5 = DR[6]; T1 = IR_LD
endmodule
